# Fritzing sketch led circuit board (saved by Fritzing 0.9.3b)
circuit board: 3cm x 3cm
breadboards: 1

parts:
  b = NPN-Transistor [package="TO92 [THT]"]
  J1 = female pin header, 4 pins [form="♀ (female)"]
  RB = Resistor [tolerance=±5% resistance=220 package=THT]
  RG = Resistor [tolerance=±5% resistance=220 package=THT]
  g = NPN-Transistor [package="TO92 [THT]"]
  r = NPN-Transistor [package="TO92 [THT]"]
  g_2 = female pin header, 1 pin [form="♀ (female)"]
  r_2 = female pin header, 1 pin [form="♀ (female)"]
  b_2 = female pin header, 1 pin [form="♀ (female)"]
  + = female pin header, 1 pin [form="♀ (female)"]
  - = female pin header, 1 pin [form="♀ (female)"]
  RR = Resistor [tolerance=±5% resistance=220 package=THT]

nets:
  N1: b.E, RB.Pin_1, RG.Pin_1, g.E, r.E, g_2.pin1, r_2.pin1, b_2.pin1, -.pin1, RR.Pin_1
  N2: b.B, J1.pin4
  N3: b.C, RB.Pin_0
  N4: J1.pin1, +.pin1
  N5: J1.pin2, g.B
  N6: J1.pin3, r.B
  N7: RG.Pin_0, g.C
  N8: r.C, RR.Pin_0
